# Fritzing sketch hamsterfitness (saved by Fritzing 0.9.3b)
circuit board: 6.6cm x 6.6cm
breadboards: 1

parts:
  OLED_display = OLED Monochrome 128x64 0.96 inch [part_number=326]
  Hall_effect_sensor = mystery part, 3 pins [chip_label=? spacing=300mil]
  Feather = Adafruit Feather M0 Bluefruit LE [part_number="Adafruit #2995"]

nets:
  N1: OLED_display.MOSI_SDA, Feather.D9
  N2: OLED_display.SCLK_SCK, Feather.D10
  N3: OLED_display.DC_SA0, Feather.D11
  N4: OLED_display.RESET, Feather.D13
  N5: OLED_display.CS, Feather.D12
  3.3V: OLED_display.3.3V, Hall_effect_sensor.pin1, Feather.+3V3
  GND: OLED_display.GND, Hall_effect_sensor.pin2, Feather.GND
  N6: Hall_effect_sensor.pin3, Feather.A0

custom parts:
  OLED Monochrome 128x64 0.96 inch: These displays are small, only about 1" diameter, but very readable due to the high contrast of an OLED display. This display is made of 128x64 individual white OLED pixels, each one is turned on or off by the controller chip. Because the display makes its own light, no backlight is required. This reduces the power required to run the OLED and is why the display has such high contrast; we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
  Adafruit Feather M0 Bluefruit LE: This is the Adafruit Feather M0 Bluefruit LE - our take on an 'all-in-one' Arduino-compatible + Bluetooth Low Energy with built in USB and battery charging. Its an Adafruit Feather M0 with a BTLE module, ready to rock! We have other boards in the Feather family, check'em out here. Bluetooth Low Energy is the hottest new low-power, 2.4GHz spectrum wireless protocol. In particular, its the only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
